# Fritzing sketch DHT_Ethernet (saved by Fritzing 0.9.2b)
breadboards: 1

parts:
  Part1 = Arduino Uno (Rev3)
  RHT1 = Humidity and Temperature Sensor RHT03
  R1 = Resistor [tolerance=±5% resistance=220 package=THT]

nets:
  N1: Part1.D7, RHT1.Data-signal, R1.Pin_0
  5V: Part1.5V, RHT1.Vcc, R1.Pin_1
  N2: Part1.GND, RHT1.GND_2

notes:
  D13=SCK, D12=SO, D11=SI, D8= CS, 3.3v=VCC, GND=GND

// code stored in the sketch: DHT22.ino
#include "DHT.h"
 
// Pin for the DHT sensor
#define DHTPIN 7    
#define DHTTYPE DHT22
// #define DHTTYPE DHT11
 
// Create instance for the DHT sensor
DHT dht(DHTPIN, DHTTYPE);

#include <EtherCard.h>
static byte mymac[] = { 0x74,0x69,0x69,0x2D,0x30,0x31 };
static byte myip[] = { 192,168,20,2 };
byte Ethernet::buffer[500];
BufferFiller bfill;


// Setup
void setup(void)
{
  dht.begin();
  Serial.begin(115200);
}
 
void loop(void)
{
    // Get command
    if (Serial.available()) {
 
      // Read command
      byte c = Serial.read ();
 
      // If a measurement is requested, measure data and send it back
      if (c == 'm'){
 
          int h = (int)dht.readHumidity();
          int t = (int)dht.readTemperature();
 
          // Send data (temperature,humidity)
          Serial.println(String(t) + "," + String(h));
      }
  }
}

// code stored in the sketch: DHT_Ethernet.ino
#include "DHT.h"
 
// Pin for the DHT sensor
#define DHTPIN 7    
#define DHTTYPE DHT22
// #define DHTTYPE DHT11
 
// Create instance for the DHT sensor
DHT dht(DHTPIN, DHTTYPE);

#include <EtherCard.h>
static byte mymac[] = { 0x74,0x69,0x69,0x2D,0x30,0x31 };
static byte myip[] = { 192,168,20,2 };
byte Ethernet::buffer[500];
BufferFiller bfill;


// Setup
void setup(void)
{
  dht.begin();
  Serial.begin(115200);
	if (ether.begin(sizeof Ethernet::buffer, mymac) == 0)
		Serial.println( "Failed to access Ethernet Controller");
	ether.staticSetup(myip);
}
 
static word homePage(){
	long t=millis() / 100;
	word h = t / 3600;
	byte m = (t / 60) % 60;
	byte s = t % 60;
	bfill = ether.tcpOffset();
	bfill.emit_p(PSTR(
		"HTTP/1.0 200 OK\r\n"
		"Content-Type: text/hmtl\r\n"
		"Pragma: no-cache\r\n"
		"\r\n"
		"<meta http-equiv='refresh' content='1'/>"
		"<title>RBBB server</title>"
		"<h1>$D$D:$D$D:$D$D<h1>"),
		h/10, h%10, m/10, m%10, s/10, s%10);
	return bfill.position();
}


void loop(void)
{

word len = ether.packetReceive();
word pos = ether.packetLoop(len);

if (pos) //check if valid tcp data is received
	ether.httpServerReply(homePage()); //send web page data


    // Get command
    if (Serial.available()) {
 
      // Read command
      byte c = Serial.read ();
 
      // If a measurement is requested, measure data and send it back
      if (c == 'm'){
 
          int h = (int)dht.readHumidity();
          int t = (int)dht.readTemperature();
 
          // Send data (temperature,humidity)
          Serial.println(String(t) + "," + String(h));
      }
  }
}
